// Digital circuit ALU.dig as structural Verilog
module ALU (
  input  [3:0] I,
  input  D,
  input  R,
  input  C_In,
  output O,
  output NOP,
  output C_Out,
  output C_En
);

  wire and_2_out, and_4_out, and_5_out, and_6_out, and_9_out, and_10_out, and_11_out, and_12_out, and_13_out,
       and_14_out, and_15_out, and_16_out, and_17_out, decoder_1_out_0, multiplexer_1_out, multiplexer_2_out,
       multiplexer_3_out, nand_1_out, not_1_out, not_2_out, not_3_out, Op_ADDSUB, Op_LD, Op_NAND, Op_OR,
       Op_XOR, or_1_out, Sig_ONOX, xor_1_out, xor_2_out, xor_3_out, xor_4_out;

  and and_1 (Op_ADDSUB, I[1], ~I[2], ~I[3]);  // And
  and and_2 (and_2_out, ~I[2], ~I[3], ~I[1]);  // And
  and and_3 (Sig_ONOX, I[2], ~I[3]);  // And
  Decoder #(.Selector_Bits(2)) decoder_1 (
    .sel(I[1:0]), .out_0(decoder_1_out_0), .out_1(Op_NAND), .out_2(Op_OR), .out_3(Op_XOR));
  not not_1 (not_1_out, R);
  and and_4 (and_4_out, I[0], Op_ADDSUB);
  Multiplexer multiplexer_1 (.sel(and_4_out), .in_0(C_In), .in_1(not_2_out), .out(multiplexer_1_out));
  not not_2 (not_2_out, C_In);
  Multiplexer multiplexer_2 (.sel(and_4_out), .in_0(R), .in_1(not_1_out), .out(multiplexer_2_out));
  // Probe Op_SUB on and_4_out
  and and_5 (and_5_out, Sig_ONOX, decoder_1_out_0);
  nand nand_1 (nand_1_out, R, D);
  or or_1 (or_1_out, R, D);
  xor xor_1 (xor_1_out, D, R);
  xor xor_2 (xor_2_out, D, multiplexer_2_out);
  and and_6 (and_6_out, multiplexer_2_out, D);
  and and_7 (Op_LD, I[0], and_2_out);
  and and_8 (NOP, ~I[0], and_2_out);  // And
  and and_9 (and_9_out, Sig_ONOX, Op_NAND);
  and and_10 (and_10_out, Sig_ONOX, Op_OR);
  xor xor_3 (xor_3_out, multiplexer_1_out, xor_2_out);
  and and_11 (and_11_out, xor_2_out, multiplexer_1_out);
  xor xor_4 (xor_4_out, and_11_out, and_6_out);
  or or_2 (C_En, Op_ADDSUB, and_5_out);
  and and_12 (and_12_out, nand_1_out, and_9_out);
  and and_13 (and_13_out, or_1_out, and_10_out);
  and and_14 (and_14_out, Op_LD, D);
  and and_15 (and_15_out, Sig_ONOX, Op_XOR, xor_1_out);
  and and_16 (and_16_out, Op_ADDSUB, xor_3_out);
  not not_3 (not_3_out, xor_4_out);
  Multiplexer multiplexer_3 (.sel(and_4_out), .in_0(xor_4_out), .in_1(not_3_out), .out(multiplexer_3_out));
  or or_3 (O, and_12_out, and_13_out, and_14_out, and_15_out, and_16_out, and_5_out);
  and and_17 (and_17_out, multiplexer_3_out, ~and_5_out);  // And
  // Probe Op_ONE on and_5_out
  and and_18 (C_Out, and_17_out, Op_ADDSUB);

  // Notes on the sheet:
  //   GN14K5-ALU
endmodule

/* Test case:
INST	A	B	C_In	Out	C_Out	C_En	NOP
#NOP
0x0	0	0	0	0	0	0	1
#LD
0x1	0	X	X	0	0	0	0	
0x1	1	X	X	1	0	0	0
#ADD
0x2	0	0	0	0	0	1	0
0x2	0	0	1	1	0	1	0
0x2	0	1	0	1	0	1	0
0x2	0	1	1	0	1	1	0
0x2	1	0	0	1	0	1	0
0x2	1	0	1	0	1	1	0
0x2	1	1	0	0	1	1	0
0x2	1	1	1	1	1	1	0
#SUB
0x3	0	0	0	0	0	1	0
0x3	0	0	1	1	1	1	0
0x3	0	1	0	1	1	1	0
0x3	0	1	1	0	1	1	0
0x3	1	0	0	1	0	1	0
0x3	1	0	1	0	0	1	0
0x3	1	1	0	0	0	1	0
0x3	1	1	1	1	1	1	0
#ONE
0x4	X	X	X	1	0	1	0
#NAND
0x5	0	0	X	1	0	0	0
0x5	0	1	X	1	0	0	0
0x5	1	0	X	1	0	0	0
0x5	1	1	X	0	0	0	0
#OR
0x6	0	0	X	0	0	0	0
0x6	0	1	X	1	0	0	0
0x6	1	0	X	1	0	0	0
0x6	1	1	X	1	0	0	0
#XOR
0x7	0	0	X	0	0	0	0
0x7	0	1	X	1	0	0	0
0x7	1	0	X	1	0	0	0
0x7	1	1	X	0	0	0	0
#STO	
0x8	X	X	X	0	0	0	0
#STOC
0x9	X	X	X	0	0	0	0
#IEN
0xA	X	X	X	0	0	0	0
#OEN
0xB	X	X	X	0	0	0	0
#JMP
0xC	X	X	X	0	0	0	0
#RET
0xD	X	X	X	0	0	0	0
#SKZ
0xE	X	X	X	0	0	0	0
#MEM
0xF	X	X	X	0	0	0	0
*/
