// Digital circuit GN14K5.dig as structural Verilog
module GN14K5 (
  input  CLK,
  input  D_I,
  input  [3:0] INST,
  input  SKP,
  output WE,
  output D_O,
  output R,
  output F,
  output IEN,
  output OEN,
  output CALL,
  output RET,
  output SKZ,
  output MEM
);

  wire alu_1_c_en, alu_1_c_out, alu_1_nop, alu_1_o, and_1_out, and_2_out, and_3_out, and_4_out, and_5_out,
       and_6_out, and_7_out, and_8_out, and_9_out, and_10_out, and_11_out, and_12_out, and_13_out,
       and_14_out, decoder_1_out_0, decoder_1_out_1, decoder_1_out_2, decoder_1_out_3, decoder_1_out_4,
       decoder_1_out_5, decoder_1_out_6, decoder_1_out_7, nor_1_out, not_1_out, or_1_out, or_2_out, or_3_out;
  wire [3:0] multiplexer_1_out;

  or or_1 (or_1_out, SKP, SKZ);
  Multiplexer #(.Bits(4)) multiplexer_1 (.sel(or_1_out), .in_0(INST), .in_1(4'b0000), .out(multiplexer_1_out));
  Decoder #(.Selector_Bits(3)) decoder_1 (
    .sel(multiplexer_1_out[2:0]), .out_0(decoder_1_out_0), .out_1(decoder_1_out_1), .out_2(decoder_1_out_2),
    .out_3(decoder_1_out_3), .out_4(decoder_1_out_4), .out_5(decoder_1_out_5), .out_6(decoder_1_out_6),
    .out_7(decoder_1_out_7));
  and and_1 (and_1_out, decoder_1_out_0, multiplexer_1_out[3]);
  and and_2 (and_2_out, decoder_1_out_1, multiplexer_1_out[3]);
  and and_3 (and_3_out, decoder_1_out_2, multiplexer_1_out[3]);
  and and_4 (and_4_out, decoder_1_out_3, multiplexer_1_out[3]);
  and and_5 (and_5_out, decoder_1_out_4, multiplexer_1_out[3]);
  and and_6 (and_6_out, decoder_1_out_5, multiplexer_1_out[3]);
  and and_7 (and_7_out, decoder_1_out_6, multiplexer_1_out[3]);
  and and_8 (and_8_out, decoder_1_out_7, multiplexer_1_out[3]);
  ALU alu_1 (
    .I(multiplexer_1_out), .D(and_9_out), .R(R), .C_In(F), .O(alu_1_o), .NOP(alu_1_nop), .C_Out(alu_1_c_out),
    .C_En(alu_1_c_en));
  nor nor_1 (nor_1_out, multiplexer_1_out[3], alu_1_nop);
  Register Result (.D(alu_1_o), .C(CLK), .en(nor_1_out), .Q(R));
  Register Carry (.D(alu_1_c_out), .C(CLK), .en(alu_1_c_en), .Q(F));
  Register Input_EN (.D(D_I), .C(CLK), .en(and_3_out), .Q(IEN));
  Register Output_EN (.D(D_I), .C(CLK), .en(and_4_out), .Q(OEN));
  and and_9 (and_9_out, IEN, D_I);
  not not_1 (not_1_out, R);
  and and_10 (and_10_out, not_1_out, and_7_out);
  or or_2 (or_2_out, and_1_out, and_2_out);
  and and_11 (and_11_out, R, and_1_out);
  and and_12 (and_12_out, not_1_out, and_2_out);
  or or_3 (or_3_out, and_1_out, and_2_out);
  D_FF u_CALL (.D(and_5_out), .C(CLK), .Q(CALL));  // open: nQ
  D_FF u_RET (.D(and_6_out), .C(CLK), .Q(RET));  // open: nQ
  D_FF u_SKZ (.D(and_10_out), .C(CLK), .Q(SKZ));  // open: nQ
  D_FF u_MEM (.D(and_8_out), .C(CLK), .Q(MEM));  // open: nQ
  and and_13 (and_13_out, ~or_2_out, R);  // And
  and and_14 (and_14_out, OEN, or_3_out);
  or or_4 (D_O, and_13_out, and_11_out, and_12_out);
  D_FF d_ff_1 (.D(and_14_out), .C(CLK), .Q(WE));  // open: nQ

  // Notes on the sheet:
  //   CLK: pin 1
  //   D_I: pin 9
  //   WE: pin 16
  //   D_O: pin 17
  //   INST: pin 7,6,5,4
  //   SKP: pin 2
  //   R: pin 19
  //   F: pin 18
  //   IEN: pin 15
  //   OEN: pin 14
  //   CALL: pin 23
  //   RET: pin 22
  //   SKZ: pin 21
  //   MEM: pin 20
endmodule
