// Digital circuit GN14K4L8.dig as structural Verilog
module GN14K4L8 (
  input  Clk,
  input  [2:0] Bit,
  input  DI,
  input  WR,
  input  [7:0] Byte,
  input  Load,
  output DO,
  output [7:0] Q
);

  wire or_1_out;
  wire [7:0] gn1r8_1_out, multiplexer_1_out;

  GN1R8 gn1r8_1 (.Byte(Q), .DI(DI), .Bit(Bit), .Out(gn1r8_1_out));
  Multiplexer #(.Bits(8)) multiplexer_1 (.sel(Load), .in_0(gn1r8_1_out), .in_1(Byte), .out(multiplexer_1_out));
  or or_1 (or_1_out, Load, WR);
  Register #(.Bits(8)) register_1 (.D(multiplexer_1_out), .C(Clk), .en(or_1_out), .Q(Q));
  GN8R1 gn8r1_1 (.Bit(Bit), .Byte(Q), .Out(DO));
endmodule
