// Digital circuit GN14K4M8.dig as structural Verilog
module GN14K4M8 (
  input  DI,
  input  WR,
  input  [7:0] Byte,
  input  Load,
  input  Clk,
  input  [3:0] Addr,
  output DO,
  output [7:0] Q
);

  wire demultiplexer_1_out_0, demultiplexer_1_out_1, gn14k4l8_1_do, gn14k4r8_1_p5;
  wire [7:0] gn14k4l8_1_q, gn14k4r8_1_p6;

  Demultiplexer demultiplexer_1 (.sel(Addr[0]), .in(WR), .out_0(demultiplexer_1_out_0), .out_1(demultiplexer_1_out_1));
  // GN14K4R8 gn14k4r8_1: pin names not known; wires that end beside it: Clk, Addr[3:1], DI, demultiplexer_1_out_0, gn14k4r8_1_p5, gn14k4r8_1_p6
  GN14K4L8 gn14k4l8_1 (
    .Clk(Clk), .Bit(Addr[3:1]), .DI(DI), .WR(demultiplexer_1_out_1), .Byte(Byte), .Load(Load),
    .DO(gn14k4l8_1_do), .Q(gn14k4l8_1_q));
  Multiplexer multiplexer_1 (.sel(Addr[0]), .in_0(gn14k4r8_1_p5), .in_1(gn14k4l8_1_do), .out(DO));
  Multiplexer #(.Bits(8)) multiplexer_2 (.sel(Addr[0]), .in_0(gn14k4r8_1_p6), .in_1(gn14k4l8_1_q), .out(Q));
endmodule
