// Digital circuit GN14K4R8.dig as structural Verilog
module GN14K4R8 (
  input  Clk,
  input  [2:0] Bit,
  input  DI,
  input  WR,
  output DO,
  output [7:0] Q
);

  wire [7:0] gn1r8_1_out;

  GN1R8 gn1r8_1 (.Byte(Q), .DI(DI), .Bit(Bit), .Out(gn1r8_1_out));
  Register #(.Bits(8)) R8 (.D(gn1r8_1_out), .C(Clk), .en(WR), .Q(Q));
  GN8R1 gn8r1_1 (.Bit(Bit), .Byte(Q), .Out(DO));
  // Pins of 1 and 8 bits meet at Q
endmodule
