// Digital circuit GN1R8.dig as structural Verilog
module GN1R8 (
  input  [7:0] Byte,
  input  DI,
  input  [2:0] Bit,
  output [7:0] Out
);

  wire [7:0] and_1_out, demultiplexer_1_out_5, demultiplexer_2_out_0, not_1_out;

  Demultiplexer #(.Selector_Bits(3)) demultiplexer_1 (
    .sel(Bit), .in(DI), .out_0(demultiplexer_1_out_5[0]), .out_1(demultiplexer_1_out_5[1]),
    .out_2(demultiplexer_1_out_5[2]), .out_3(demultiplexer_1_out_5[3]), .out_4(demultiplexer_1_out_5[4]),
    .out_5(demultiplexer_1_out_5[5]), .out_6(demultiplexer_1_out_5[6]), .out_7(demultiplexer_1_out_5[7]));
  Demultiplexer #(.Selector_Bits(3)) demultiplexer_2 (
    .sel(Bit), .in(1'b1), .out_0(demultiplexer_2_out_0[0]), .out_1(demultiplexer_2_out_0[1]),
    .out_2(demultiplexer_2_out_0[2]), .out_3(demultiplexer_2_out_0[3]), .out_4(demultiplexer_2_out_0[4]),
    .out_5(demultiplexer_2_out_0[5]), .out_6(demultiplexer_2_out_0[6]), .out_7(demultiplexer_2_out_0[7]));
  assign not_1_out = ~demultiplexer_2_out_0;  // Not not_1, 8 bits wide
  assign and_1_out = Byte & not_1_out;  // And and_1, 8 bits wide
  assign Out = demultiplexer_1_out_5 | and_1_out;  // Or or_1, 8 bits wide
endmodule

/* Test case:
DI	Byte	Bit	Out
0	0xFF	0	0b11111110
0	0xFF	1	0b11111101
0	0xFF	2	0b11111011
0	0xFF	3	0b11110111
0	0xFF	4	0b11101111
0	0xFF	5	0b11011111
0	0xFF	6	0b10111111
0	0xFF	7	0b01111111
1	0	0	0b00000001
1	0	1	0b00000010
1	0	2	0b00000100
1	0	3	0b00001000
1	0	4	0b00010000
1	0	5	0b00100000
1	0	6	0b01000000
1	0	7	0b10000000
*/
