// Digital circuit GN2CLK.dig as structural Verilog
module GN2CLK (
  input  Trigger,
  input  Clk,
  output Clk_2,
  output _2Clk
);

  wire d_ff_1_q;

  D_FF d_ff_1 (.D(Trigger), .C(Clk), .Q(d_ff_1_q));  // open: nQ
  D_FF d_ff_2 (.D(d_ff_1_q), .C(Clk), .Q(Clk_2));  // open: nQ

  assign _2Clk = Clk;
endmodule
