// Digital circuit GN8R1.dig as structural Verilog
module GN8R1 (
  input  [2:0] Bit,
  input  [7:0] Byte,
  output Out
);

  wire and_1_out, and_2_out, and_3_out, and_4_out, and_5_out, and_6_out, and_7_out, and_8_out,
       demultiplexer_1_out_0, demultiplexer_1_out_1, demultiplexer_1_out_2, demultiplexer_1_out_3,
       demultiplexer_1_out_4, demultiplexer_1_out_5, demultiplexer_1_out_6, demultiplexer_1_out_7;

  Demultiplexer #(.Selector_Bits(3)) demultiplexer_1 (
    .sel(Bit), .in(1'b1), .out_0(demultiplexer_1_out_0), .out_1(demultiplexer_1_out_1),
    .out_2(demultiplexer_1_out_2), .out_3(demultiplexer_1_out_3), .out_4(demultiplexer_1_out_4),
    .out_5(demultiplexer_1_out_5), .out_6(demultiplexer_1_out_6), .out_7(demultiplexer_1_out_7));
  and and_1 (and_1_out, demultiplexer_1_out_0, Byte[0]);
  and and_2 (and_2_out, demultiplexer_1_out_1, Byte[1]);
  and and_3 (and_3_out, demultiplexer_1_out_2, Byte[2]);
  and and_4 (and_4_out, demultiplexer_1_out_3, Byte[3]);
  and and_5 (and_5_out, demultiplexer_1_out_4, Byte[4]);
  and and_6 (and_6_out, demultiplexer_1_out_5, Byte[5]);
  and and_7 (and_7_out, demultiplexer_1_out_6, Byte[6]);
  and and_8 (and_8_out, demultiplexer_1_out_7, Byte[7]);
  or or_1 (Out, and_1_out, and_2_out, and_3_out, and_4_out, and_5_out, and_6_out, and_7_out, and_8_out);
endmodule

/* Test case:
Bit	Byte	Out
0x0	0xAA	0x0
0x1	0xAA	0x1
0x2	0xAA	0x0
0x3	0xAA	0x1
0x4	0xAA	0x0
0x5	0xAA	0x1
0x6	0xAA	0x0
0x7	0xAA	0x1
*/
