// Digital circuit GN14K5.dig as structural Verilog
module GN14K5 (
  input  CLK,
  input  DI,
  input  [3:0] INST,
  input  nRST,
  output WE,
  output MEM,
  output RBT,
  output HLT,
  output JMP,
  output RET,
  output DO,
  output C,
  output R,
  output SKZ
);

  wire alu_1_c_en, alu_1_c_out, alu_1_nop, alu_1_o, and_1_out, and_2_out, and_3_out, and_4_out, and_5_out,
       and_6_out, and_7_out, and_8_out, and_9_out, decoder_1_out_0, decoder_1_out_1, decoder_1_out_2,
       decoder_1_out_3, decoder_1_out_4, decoder_1_out_5, decoder_1_out_6, decoder_1_out_7, nor_1_out,
       not_1_out, or_1_out;
  wire [3:0] multiplexer_1_out;

  Multiplexer #(.Bits(4)) multiplexer_1 (.sel(SKZ), .in_0(INST), .in_1(4'b0000), .out(multiplexer_1_out));
  Decoder #(.Selector_Bits(3)) decoder_1 (
    .sel(multiplexer_1_out[2:0]), .out_0(decoder_1_out_0), .out_1(decoder_1_out_1), .out_2(decoder_1_out_2),
    .out_3(decoder_1_out_3), .out_4(decoder_1_out_4), .out_5(decoder_1_out_5), .out_6(decoder_1_out_6),
    .out_7(decoder_1_out_7));
  and and_1 (and_1_out, decoder_1_out_0, multiplexer_1_out[3]);
  and and_2 (and_2_out, decoder_1_out_1, multiplexer_1_out[3]);
  and and_3 (and_3_out, decoder_1_out_2, multiplexer_1_out[3]);
  and and_4 (and_4_out, decoder_1_out_3, multiplexer_1_out[3]);
  and and_5 (and_5_out, decoder_1_out_4, multiplexer_1_out[3]);
  and and_6 (and_6_out, decoder_1_out_5, multiplexer_1_out[3]);
  and and_7 (and_7_out, decoder_1_out_6, multiplexer_1_out[3]);
  and and_8 (and_8_out, decoder_1_out_7, multiplexer_1_out[3]);
  ALU alu_1 (
    .I(multiplexer_1_out), .D(DI), .R(R), .C_In(C), .O(alu_1_o), .NOP(alu_1_nop), .C_Out(alu_1_c_out),
    .C_En(alu_1_c_en));
  nor nor_1 (nor_1_out, multiplexer_1_out[3], alu_1_nop);
  Register Result (.D(alu_1_o), .C(CLK), .en(nor_1_out), .Q(R));
  Register Carry (.D(alu_1_c_out), .C(CLK), .en(alu_1_c_en), .Q(C));
  not not_1 (not_1_out, R);
  Multiplexer multiplexer_2 (.sel(and_2_out), .in_0(R), .in_1(not_1_out), .out(DO));
  or or_1 (or_1_out, and_1_out, and_2_out);
  and and_9 (and_9_out, not_1_out, and_6_out);
  D_FF u_WE (.D(or_1_out), .C(CLK), .Q(WE));  // open: nQ
  D_FF u_JMP (.D(and_3_out), .C(CLK), .Q(JMP));  // open: nQ
  D_FF u_RET (.D(and_4_out), .C(CLK), .Q(RET));  // open: nQ
  D_FF u_MEM (.D(and_5_out), .C(CLK), .Q(MEM));  // open: nQ
  D_FF u_SKZ (.D(and_9_out), .C(CLK), .Q(SKZ));  // open: nQ
  D_FF u_RBT (.D(and_7_out), .C(CLK), .Q(RBT));  // open: nQ
  D_FF u_HLT (.D(and_8_out), .C(CLK), .Q(HLT));  // open: nQ

  // Notes on the sheet:
  //   CLK: pin 1
  //   DI: pin 2
  //   WE: pin 22
  //   INST: pin 3,4,5,6
  //   MEM: pin 17
  //   RBT: pin 15
  //   HLT: pin 14
  //   JMP: pin 19
  //   RET: pin 18
  //   DO: pin 23
  //   C: pin 20
  //   R: pin 21
  //   SKZ: pin 16
  //   nRST: pin 7
endmodule

/* Test case:
CLK INST DI	R C DO WE JMP RET MEM SKZ RBT HLT
# NOP
0   0x0  0	0 0 0  0   0   0   0   0   0   0 
1   0x0  0	0 0 0  0   0   0   0   0   0   0 

# STO
0   0x8  0	0 x x  x   x   x   x   x   x   x
1   0x8  0	0 0 0  1   0   0   0   0   0   0 

# STOI
#0   0x9  0	0 x x  1   x   x   x   x   x   x
#1   0x9  0	0 0 0  1   0   0   0   0   0   0 

# SKZ
0   0xD  0	0 x x  x   x   x   x   0   x   x
1   0xD  0	0 x x  0   0   0   0   1   0   0

# NOP (skipped)
0   0x0  0	0 0 0  0   0   0   0   1   0   0 
1   0x0  0	0 0 0  0   0   0   0   0   0   0

# ONE 
0   0x4  0	0 x x  x   x   x   x   x   x   x
1   0x4  0	1 0 x  x   x   x   x   x   x   x

# SKZ (no skip)
0   0xD  0	1 x x  x   x   x   x   0   x   x
1   0xD  0	1 x x  0   0   0   0   0   0   0

# LD
0   0x1  0	x x x  x   x   x   x   x   x   x
1   0x1  0	0 x 0  0   0   0   0   0   0   0
0   0x1  1	x x x  x   x   x   x   x   x   x
1   0x1  1	1 x 1  0   0   0   0   0   0   0

# JMP
0   0xA  0	x x x  x   x   x   x   x   x   x
1   0xA  0	x x x  0   1   0   0   0   0   0

# RET
0   0xB  0	x x x  x   x   x   x   x   x   x
1   0xB  0	x x x  0   0   1   0   0   0   0

# MEM
0   0xC  0	x x x  x   x   x   x   x   x   x
1   0xC  0	x x x  0   0   0   1   0   0   0

# RBT
0   0xE  0	x x x  x   x   x   x   x   x   x
1   0xE  0	x x x  0   0   0   0   0   1   0

# HLT
0   0xF  0	x x x  x   x   x   x   x   x   x
1   0xF  0	x x x  0   0   0   0   0   0   1

# ADD
0   0x2  0	1 0 1  x   x   x   x   x   x   x
1   0x2  0	1 0 1  0   0   0   0   0   0   0
0   0x2  1	1 0 1  x   x   x   x   x   x   x
1   0x2  1	0 1 0  0   0   0   0   0   0   0
0   0x2  1	0 1 0  x   x   x   x   x   x   x
1   0x2  1	0 1 0  0   0   0   0   0   0   0
0   0x2  0	0 1 0  x   x   x   x   x   x   x
1   0x2  0	1 0 1  0   0   0   0   0   0   0

# SUB
0   0x3  0	1 0 1  x   x   x   x   x   x   x
1   0x3  0	1 1 1  0   0   0   0   0   0   0
0   0x3  0	1 1 1  x   x   x   x   x   x   x
1   0x3  0	0 1 0  0   0   0   0   0   0   0
0   0x3  1	0 1 0  x   x   x   x   x   x   x
1   0x3  1	0 0 0  0   0   0   0   0   0   0
0   0x3  1	0 0 0  x   x   x   x   x   x   x
1   0x3  1	1 0 1  0   0   0   0   0   0   0

# NAND
0   0x5  0	1 x 1  x   x   x   x   x   x   x
1   0x5  0	1 x 1  0   0   0   0   0   0   0
0   0x5  1	1 x 1  x   x   x   x   x   x   x
1   0x5  1	0 x 0  0   0   0   0   0   0   0
0   0x5  1	0 x 0  x   x   x   x   x   x   x
1   0x5  1	1 x 1  0   0   0   0   0   0   0
0   0x5  1	1 x 1  x   x   x   x   x   x   x
1   0x5  1	0 x 0  0   0   0   0   0   0   0

# OR
0   0x6  1	0 x 0  x   x   x   x   x   x   x
1   0x6  1	1 x 1  0   0   0   0   0   0   0
0   0x5  1	1 x 1  x   x   x   x   x   x   x
1   0x5  1	0 x 0  0   0   0   0   0   0   0
0   0x6  0	0 x 0  x   x   x   x   x   x   x
1   0x6  0	0 x 0  0   0   0   0   0   0   0
0   0x6  1	0 x 0  x   x   x   x   x   x   x
1   0x6  1	1 x 1  0   0   0   0   0   0   0
0   0x6  0	1 x 1  x   x   x   x   x   x   x
1   0x6  0	1 x 1  0   0   0   0   0   0   0

# XOR
0   0x7  0	1 x 1  x   x   x   x   x   x   x
1   0x7  0	1 x 1  0   0   0   0   0   0   0
0   0x7  1	1 x 1  x   x   x   x   x   x   x
1   0x7  1	0 x 0  0   0   0   0   0   0   0
0   0x7  1	0 x 0  x   x   x   x   x   x   x
1   0x7  1	1 x 1  0   0   0   0   0   0   0
*/
