// Digital circuit Testsys.dig as structural Verilog
module Testsys (
  input  clk
);

  wire comparator_1_eq, gn14k5_1_c, gn14k5_1_do, gn14k5_1_hlt, gn14k5_1_jmp, gn14k5_1_mem, gn14k5_1_r,
       gn14k5_1_rbt, gn14k5_1_ret, gn14k5_1_skz, gn14k5_1_we, not_1_out;
  wire [4:0] Testcode_d;
  wire [7:0] counter_1_out;

  not not_1 (not_1_out, clk);
  Counter #(.Bits(8)) counter_1 (.en(1'b1), .C(clk), .clr(comparator_1_eq), .out(counter_1_out));  // open: ovf
  Comparator #(.Bits(8)) comparator_1 (.a(8'h4), .b(counter_1_out), .eq(comparator_1_eq));  // open: gt, lt
  ROM #(.AddrBits(8), .Bits(5)) Testcode (.A(counter_1_out), .sel(1'b1), .D(Testcode_d));
  GN14K5 gn14k5_1 (
    .CLK(not_1_out), .DI(Testcode_d[0]), .INST(Testcode_d[4:1]), .DO(gn14k5_1_do), .WE(gn14k5_1_we),
    .R(gn14k5_1_r), .C(gn14k5_1_c), .JMP(gn14k5_1_jmp), .RET(gn14k5_1_ret), .MEM(gn14k5_1_mem),
    .SKZ(gn14k5_1_skz), .RBT(gn14k5_1_rbt), .HLT(gn14k5_1_hlt));

  // Notes on the sheet:
  //   contents of Testcode (hex, n*v repeats v):
  //   16,19,17,1c
endmodule
